# Fritzing sketch charlie (saved by Fritzing 0.9.3b)
circuit board: 11.951cm x 6.76401cm

parts:
  Součástka1 = Arduino Pro Mini v13
  Součástka2 = Thumb Joystick
  Nokia_5110_LCD_Module1 = Nokia 5110 LCD
  S1 = Pushbutton [package="[THT]"]
  S2 = Pushbutton [package="[THT]"]

nets:
  GND: Součástka1.GND, Součástka2.GND, Nokia_5110_LCD_Module1.GND, Nokia_5110_LCD_Module1.LED_(out), S1.Pin_3, S1.Pin_4, S2.Pin_3, S2.Pin_4
  VCC: Součástka1.VCC, Součástka2.VCC, Nokia_5110_LCD_Module1.Vcc, Nokia_5110_LCD_Module1.BL, Nokia_5110_LCD_Module1.DN(MODI)_(out), Nokia_5110_LCD_Module1.SCLK_(out)
  N1: Součástka1.A3, S1.Pin_1, S1.Pin_2
  N2: Součástka1.A2, S2.Pin_1, S2.Pin_2
  N3: Součástka1.A1, Součástka2.VERT
  N4: Součástka1.A0, Součástka2.HORZ
  N5: Součástka1.D6_PWM, Nokia_5110_LCD_Module1.Clk
  N6: Součástka1.D5_PWM, Nokia_5110_LCD_Module1.Din
  N7: Součástka1.D4, Nokia_5110_LCD_Module1.DC
  N8: Součástka1.D3_PWM, Nokia_5110_LCD_Module1.CE
  N9: Součástka1.D2, Nokia_5110_LCD_Module1.RST

custom parts:
  Nokia 5110 LCD: Nokia 5110 Graphic 84*48 LCD module such as the Sparkfun LCD-10168 or the clones from Ebay. There is example code for the Arduino available from the Sparkfun site in https://learn.sparkfun.com/tutorials/graphic-lcd-hookup-guide This is a 3.3V device, if you are running it from a 5V micro you need a 5V tolorant level translator such as the 74ahc367 to protect the signal imputs. Rafa G. did a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
